# Fritzing sketch ATtiny_941_board (saved by Fritzing 0.9.3b)
perfboards: 1

parts:
  U1 = ATTINY45 [package=dip]
  U3 = ATTINY45 [package=dip]
  U2 = ATTINY45 [package=dip]
  Bauteil1 = Logic Level Converter
  Raspberry_Pi_1 = Raspberry Pi 3 [part_number=RPI-3-V1.2]
  R1 = Resistor [tolerance=±5% resistance=4.7k package=THT]
  R2 = Resistor [tolerance=±5% resistance=4.7k package=THT]
  S1 = Round Pushbutton
  LED1 = LED - 5mm [color="Red (633nm)" package="5 mm [THT]"]

nets:
  GND: U1.GND, U3.GND, U2.GND, Bauteil1.GND, Raspberry_Pi_1.GND, LED1.cathode
  N1: U1.PB0(MOSI), U3.PB0(MOSI), U2.PB0(MOSI), Bauteil1.RX2_HV, R1.Pin_1
  N2: U1.PB2(SCK_ADC1), U3.PB2(SCK_ADC1), U2.PB2(SCK_ADC1), Bauteil1.TX2_HV, R2.Pin_1
  VCC: U1.VCC, U3.VCC, U2.VCC, Bauteil1.HV, Raspberry_Pi_1.5V, R1.Pin_0, R2.Pin_0
  N3: Bauteil1.TX2_LV, Raspberry_Pi_1.GPIO3
  N4: Bauteil1.RX2_LV, Raspberry_Pi_1.GPIO2
  N5: Raspberry_Pi_1.GPIO26, LED1.anode
  N6: Raspberry_Pi_1.GPIO21, S1.leg1

notes:
  RDM 6300
  Buttons
  Rotary
  RDM6300 - ATTiny
  Pin 2 - Pin 2
  Pin 3 - Pin 3
  Play/Pause
  Prev
  Next
  CLK
  DT
  SW
  blue: sda
  green: scl
